# Fritzing sketch game_of_life (saved by Fritzing 0.8.0b)
breadboards: 1

parts:
  Nokia_5110_LCD_Module2 = Nokia5110LCDModule
  Part1 = Arduino Uno (Rev3)
  S2 = Pushbutton [package="[SMD]"]
  R1 = Resistor [tolerance=±5% resistance=4.7k package=THT]

nets:
  N1: Nokia_5110_LCD_Module2.Vcc, Part1.D7
  N2: Nokia_5110_LCD_Module2.Grnd, Part1.D6_PWM
  N3: Nokia_5110_LCD_Module2.SCE, Part1.D5_PWM
  N4: Nokia_5110_LCD_Module2.RST, Part1.D4
  N5: Nokia_5110_LCD_Module2.D/C, Part1.D3_PWM
  N6: Nokia_5110_LCD_Module2.6_DN_(MOSI), Part1.3V3, S2.Pin_1, S2.Pin_2
  N7: Nokia_5110_LCD_Module2.SCLK, Part1.D8
  N8: Nokia_5110_LCD_Module2.LED, Part1.GND, R1.Pin_0
  N9: Part1.D2, S2.Pin_3, S2.Pin_4, R1.Pin_1

custom parts:
  : Nokia 5110 LCD with 8 pin. It's a 45mm*45mm module part. Description: The Nokia 5110 is a basic graphic LCD screen for lots of applications. It was originally intended for as a cell phone screen. This one is mounted on an easy to solder PCB. It uses the PCD8544 controller. The PCD8544 is a low power CMOS LCD controller/driver, designed to drive a graphic display of 48 rows and 84 columns. All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
